// Logisim project Zhuge_Yuxuan.circ as structural Verilog: 13 circuits, main circuit main
module main (
  output [1:0] res_1,
  output [31:0] out_2,
  output [31:0] res_1_2,
  output [31:0] out_4,
  output [31:0] halt,
  output [31:0] A0,
  output [31:0] A1,
  output [31:0] A2,
  output [3:0] res_1_3,
  output [31:0] halt_2
);

  wire _1, _2, chkz, CLK, CLOCK_out, comparator_1_eq, d_ff_1_q, EX__NOP, halt_t, ID_RR__NOP, ID_Rx, JALR,
       LdMEM, MEM_ADDRESS, MEM_NOP, MEM_RES, not_1_out, Offset_Rz_Rx, PC_Data, Rx_VAL, squash, Stall,
       WB__NOP, WB_Ry, WrEn, WrMEM;
  wire [0:0] multiplexer_10_out;
  wire [3:0] EX_Opcode, idrr_ex_buffer_1_rx_out, idrr_ex_buffer_1_ry2_out, mem_wb_buffer_1_rx4_out,
       mem_wb_buffer_1_ry4_out, Opcode, Rx, Ry, WB__Opcode, WrRegNO;
  wire [19:0] idrr_ex_buffer_1_offset2_out;
  wire [23:0] Address, controlled_buffer_1_out;
  wire [31:0] adder_1_out, adder_2_out, bit_extender_1_out, controlled_buffer_2_out,
       dual_ported_register_file_1_out1, dual_ported_register_file_1_out2, EX_PC, EX_res,
       idrr_ex_buffer_1_ry_2_out, if_idrr_buffer_1_pc1_out, MEM__Rx, mem_ins, mem_out, MEM_PC,
       mem_wb_buffer_1_d4_out, mem_wb_buffer_1_rx_4_out, multiplexer_1_out, multiplexer_2_out,
       multiplexer_3_out, multiplexer_6_out, multiplexer_7_out, multiplexer_9_out, PC_q, res_1_t, res_2,
       Result, Rx_t, WB__RES, wb_ins;

  Register #(.width(32)) PC (.D(multiplexer_2_out), .Q(PC_q), .clk(CLK));  // open: en, clr
  Multiplexer #(.width(32)) multiplexer_1 (
    .in0(32'h1), .in1({32{1'b0}}), .out(multiplexer_1_out), .sel(Stall));  // open: en
  Multiplexer #(.select(2), .width(32)) multiplexer_2 (
    .in0(adder_1_out), .in1(adder_2_out), .in2(Rx_t), .out(multiplexer_2_out),
    .sel({JALR, multiplexer_10_out[0]}));  // open: in3, en
  Adder #(.width(32)) adder_1 (.a(multiplexer_1_out), .b(PC_q), .out(adder_1_out));  // open: cin, cout
  RAM #(.addrWidth(24), .dataWidth(32)) ram_1 (.addr(PC_q[23:0]), .data(out_4), .clk(CLK));  // open: sel, ld, clr
  assign controlled_buffer_1_out = MEM_ADDRESS ? Address : 24'bz;  // Controlled_Buffer controlled_buffer_1
  ID_RR_Controller ID_RR_Controller (.Opcode(out_2[31:28]), .Rx_Rz(ID_Rx));
  assign controlled_buffer_2_out = MEM_RES ? Result : 32'bz;  // Controlled_Buffer controlled_buffer_2
  IF_IDRR_Buffer if_idrr_buffer_1 (
    .NOP1(Stall), .PC(adder_1_out), .In1(out_4), .Clk(CLK), .NOP1_out(ID_RR__NOP),
    .PC1_out(if_idrr_buffer_1_pc1_out), .Out1(out_2), .squash(squash));
  D_Flip_Flop d_ff_1 (.clk(halt_t), .D(CLOCK_out), .Q(d_ff_1_q));  // open: Qn, preset, en, reset
  not not_1 (not_1_out, WrMEM);
  assign mem_out = LdMEM ? multiplexer_3_out : 32'bz;  // Controlled_Buffer controlled_buffer_3
  Multiplexer #(.width(32)) multiplexer_3 (
    .in0(controlled_buffer_2_out), .in1(MEM__Rx), .out(multiplexer_3_out), .sel(Rx_VAL));  // open: en
  and and_1 (CLK, ~d_ff_1_q, CLOCK_out);  // AND_Gate
  Clock CLOCK (.out(CLOCK_out));
  RAM #(.addrWidth(24), .dataWidth(32)) ram_2 (
    .addr(controlled_buffer_1_out), .data(mem_out), .clk(CLK), .ld(not_1_out));  // open: sel, clr
  EX_Controller EX__Controller (
    .NOP(EX__NOP), .Opcode(EX_Opcode), .Offset_Rz(Offset_Rz_Rx), .jalr(JALR), .chkz(chkz), .Func(res_1));
  Multiplexer #(.width(4)) multiplexer_4 (
    .in0(out_2[3:0]), .in1(out_2[27:24]), .out(res_1_3), .sel(ID_Rx));  // open: en
  MEM_WB_Buffer mem_wb_buffer_1 (
    .NOP4(MEM_NOP), .Opcode4(Opcode), .D4(mem_out), .Rx4(Rx), .Ry4(Ry), .Rx_4(MEM__Rx), .PC4(MEM_PC),
    .ins4(mem_ins), .CLK(CLK), .NOP4_out(WB__NOP), .Opcode4_out(WB__Opcode), .D4_out(mem_wb_buffer_1_d4_out),
    .Rx4_out(mem_wb_buffer_1_rx4_out), .Ry4_out(mem_wb_buffer_1_ry4_out),
    .Rx_4_out(mem_wb_buffer_1_rx_4_out), .ins4_out(wb_ins));  // open: PC4_out
  Multiplexer #(.width(4)) multiplexer_5 (
    .in0(mem_wb_buffer_1_rx4_out), .in1(mem_wb_buffer_1_ry4_out), .out(WrRegNO), .sel(WB_Ry));  // open: en
  MEM_Controller MEM_Controller (
    .NOP(MEM_NOP), .Opcode(Opcode), .mem_address(MEM_ADDRESS), .mem_res(MEM_RES), .rx_val(Rx_VAL),
    .WrMem(WrMEM), .LdMem(LdMEM));
  Dual_Ported_Register_File dual_ported_register_file_1 (
    .CLK(CLK), .WrEN(WrEn), .OUT1(dual_ported_register_file_1_out1), .WrREGNO(WrRegNO),
    .RdREGNO1(out_2[23:20]), .RdREGNO2(res_1_3), .OUT2(dual_ported_register_file_1_out2), .INPUT(WB__RES),
    .a0(A0), .a1(A1), .a2(A2));
  Multiplexer #(.width(32)) multiplexer_6 (
    .in0(dual_ported_register_file_1_out2), .in1(res_2), .out(multiplexer_6_out), .sel(_2));  // open: en
  Multiplexer #(.width(32)) multiplexer_7 (
    .in0(dual_ported_register_file_1_out1), .in1(res_1_t), .out(multiplexer_7_out), .sel(_1));  // open: en
  Multiplexer #(.width(32)) multiplexer_8 (
    .in0(mem_wb_buffer_1_d4_out), .in1(mem_wb_buffer_1_rx_4_out), .out(WB__RES), .sel(PC_Data));  // open: en
  IDRR_EX_Buffer idrr_ex_buffer_1 (
    .NOP(ID_RR__NOP), .Opcode2(out_2[31:28]), .Ry_2(multiplexer_7_out), .Rz___Rx_2(multiplexer_6_out),
    .Offset2(out_2[19:0]), .PC(if_idrr_buffer_1_pc1_out), .Rx2(out_2[27:24]), .Ry2(out_2[23:20]),
    .instruction2(out_2), .squash2(ID_RR__NOP), .CLK(CLK), .NOP2_out(EX__NOP), .Opcode2_out(EX_Opcode),
    .Ry_2_out(idrr_ex_buffer_1_ry_2_out), .Rz___Rx_2_out(Rx_t), .Offset2_out(idrr_ex_buffer_1_offset2_out),
    .PC2_out(EX_PC), .Rx_out(idrr_ex_buffer_1_rx_out), .Ry2_out(idrr_ex_buffer_1_ry2_out),
    .instruction2_out(res_1_2));
  WB_Controller WB_Controller (
    .NOP(WB__NOP), .Opcode(WB__Opcode), .halt(halt_t), .PC_DATA(PC_Data), .WrEn(WrEn), .WB_Ry(WB_Ry));
  or or_1 (squash, multiplexer_10_out[0], JALR);
  assign bit_extender_1_out = {{12{idrr_ex_buffer_1_offset2_out[19]}}, idrr_ex_buffer_1_offset2_out};  // Bit_Extender bit_extender_1
  Adder #(.width(32)) adder_2 (.a(EX_PC), .b(bit_extender_1_out), .out(adder_2_out));  // open: cin, cout
  Multiplexer #(.width(32)) multiplexer_9 (
    .in0(Rx_t), .in1(bit_extender_1_out), .out(multiplexer_9_out), .sel(Offset_Rz_Rx));  // open: en
  forwarding_unit Forwaring_Unit (
    .RDReg_1(out_2[23:20]), .RDReg_2(res_1_3), .EX_Instruction(res_1_2), .EX_INPUT(EX_res),
    .MEM_Instruction(mem_ins), .MEM_INPUT(mem_out), .WB_Instruction(wb_ins), .WB_INPUT(WB__RES),
    .STALL(Stall), ._1(_1), ._1_2(res_1_t), ._2(res_2), ._2_2(_2));
  Multiplexer multiplexer_10 (.in0(1'b0), .in1(comparator_1_eq), .out(multiplexer_10_out[0]), .sel(chkz));  // open: en
  ALU alu_1 (.FUNC(res_1), .A(idrr_ex_buffer_1_ry_2_out), .OUT(EX_res), .B(multiplexer_9_out));
  Comparator #(.width(32)) comparator_1 (.a({32{1'b0}}), .b(EX_res), .eq(comparator_1_eq));  // open: gt, lt
  EX_MEM_Buffer ex_mem_buffer_1 (
    .NOP(EX__NOP), .Opcode3(EX_Opcode), .Result3(EX_res), .Address3(EX_res[23:0]),
    .Rx3(idrr_ex_buffer_1_rx_out), .Ry3(idrr_ex_buffer_1_ry2_out), .Rx_3(Rx_t), .PC3(EX_PC),
    .mem_ins3(res_1_2), .CLK(CLK), .NOP_2(MEM_NOP), .Opcode3_out(Opcode), .Result3_out(Result),
    .Address3_out(Address), .Rx3_out(Rx), .Ry_out(Ry), .Rx_3_out(MEM__Rx), .PC3_out(MEM_PC),
    .mem_ins3_out(mem_ins));

  // Other names for the same wires on the sheet: instruction[31:0] = out_2; ex_instruction[31:0] = res_1_2;
  //   Func[1:0] = res_1; r1[3:0] = out_2[23:20]; ID_RR_Opcode[3:0] = out_2[31:28]; r2[3:0] = res_1_3

  // Notes on the sheet:
  //   Disconnect here
endmodule

module Dual_Ported_Register_File (
  input  CLK,
  input  WrEN,
  input  [3:0] WrREGNO,
  input  [3:0] RdREGNO1,
  input  [3:0] RdREGNO2,
  input  [31:0] INPUT,
  output [31:0] OUT1,
  output [31:0] OUT2,
  output [31:0] a2,
  output [31:0] a0,
  output [31:0] a1
);

  wire En_a0, En_a1, En_a2, En_a3, En_a4, En_at, En_fp, En_k0, En_ra, En_s0, En_s1, En_s2, En_s3, En_sp,
       En_v0;
  wire [31:0] a3, a4, at, fp, k0, ra, s0, s1, s2, s3, sp, v0, zero;

  Decoder #(.select(4), .disabled(0)) decoder_1 (
    .out1(En_at), .out2(En_v0), .out3(En_a0), .out4(En_a1), .out5(En_a2), .out6(En_a3), .out7(En_a4),
    .out8(En_s0), .out9(En_s1), .out10(En_s2), .out11(En_s3), .out12(En_k0), .out13(En_sp), .out14(En_fp),
    .out15(En_ra), .sel(WrREGNO), .en(WrEN));  // open: out0
  Register #(.width(32)) u_zero (.D(INPUT), .en(1'b0), .Q(zero), .clk(CLK));  // open: clr
  Register #(.width(32)) u_at (.D(INPUT), .en(En_at), .Q(at), .clk(CLK));  // open: clr
  Register #(.width(32)) u_v0 (.D(INPUT), .en(En_v0), .Q(v0), .clk(CLK));  // open: clr
  Register #(.width(32)) u_a0 (.D(INPUT), .en(En_a0), .Q(a0), .clk(CLK));  // open: clr
  Register #(.width(32)) u_a1 (.D(INPUT), .en(En_a1), .Q(a1), .clk(CLK));  // open: clr
  Register #(.width(32)) u_a2 (.D(INPUT), .en(En_a2), .Q(a2), .clk(CLK));  // open: clr
  Register #(.width(32)) u_a3 (.D(INPUT), .en(En_a3), .Q(a3), .clk(CLK));  // open: clr
  Register #(.width(32)) u_a4 (.D(INPUT), .en(En_a4), .Q(a4), .clk(CLK));  // open: clr
  Multiplexer #(.select(4), .width(32), .disabled(0), .enable("false")) multiplexer_1 (
    .in0(zero), .in1(at), .in2(v0), .in3(a0), .in4(a1), .in5(a2), .in6(a3), .in7(a4), .in8(s0), .in9(s1),
    .in10(s2), .in11(s3), .in12(k0), .in13(sp), .in14(fp), .in15(ra), .out(OUT2), .sel(RdREGNO2));
  Register #(.width(32)) u_s0 (.D(INPUT), .en(En_s0), .Q(s0), .clk(CLK));  // open: clr
  Register #(.width(32)) u_s1 (.D(INPUT), .en(En_s1), .Q(s1), .clk(CLK));  // open: clr
  Register #(.width(32)) u_s2 (.D(INPUT), .en(En_s2), .Q(s2), .clk(CLK));  // open: clr
  Register #(.width(32)) u_s3 (.D(INPUT), .en(En_s3), .Q(s3), .clk(CLK));  // open: clr
  Register #(.width(32)) u_k0 (.D(INPUT), .en(En_k0), .Q(k0), .clk(CLK));  // open: clr
  Register #(.width(32)) u_sp (.D(INPUT), .en(En_sp), .Q(sp), .clk(CLK));  // open: clr
  Register #(.width(32)) u_fp (.D(INPUT), .en(En_fp), .Q(fp), .clk(CLK));  // open: clr
  Register #(.width(32)) u_ra (.D(INPUT), .en(En_ra), .Q(ra), .clk(CLK));  // open: clr
  Multiplexer #(.select(4), .width(32), .disabled(0), .enable("false")) multiplexer_2 (
    .in0(zero), .in1(at), .in2(v0), .in3(a0), .in4(a1), .in5(a2), .in6(a3), .in7(a4), .in8(s0), .in9(s1),
    .in10(s2), .in11(s3), .in12(k0), .in13(sp), .in14(fp), .in15(ra), .out(OUT1), .sel(RdREGNO1));

  // Notes on the sheet:
  //   DO NOT MODIFY THIS FILE
endmodule

module IF_IDRR_Buffer (
  input  squash,
  input  NOP1,
  input  [31:0] PC,
  input  [31:0] In1,
  input  Clk,
  output NOP1_out,
  output [31:0] PC1_out,
  output [31:0] Out1
);

  wire not_1_out;

  not not_1 (not_1_out, NOP1);
  Register #(.width(1)) NOP (.D(NOP1), .Q(NOP1_out), .clk(Clk));  // open: en, clr
  Register #(.width(32)) u_PC (.D(PC), .en(not_1_out), .Q(PC1_out), .clk(Clk), .clr(squash));
  Register #(.width(32)) IR (.D(In1), .en(not_1_out), .Q(Out1), .clk(Clk), .clr(squash));
endmodule

module IDRR_EX_Buffer (
  input  squash2,
  input  NOP,
  input  [3:0] Opcode2,
  input  [31:0] Ry_2,
  input  [31:0] Rz___Rx_2,
  input  [19:0] Offset2,
  input  [31:0] PC,
  input  [3:0] Rx2,
  input  [3:0] Ry2,
  input  [31:0] instruction2,
  input  CLK,
  output NOP2_out,
  output [3:0] Opcode2_out,
  output [31:0] Ry_2_out,
  output [31:0] Rz___Rx_2_out,
  output [19:0] Offset2_out,
  output [31:0] PC2_out,
  output [3:0] Rx_out,
  output [3:0] Ry2_out,
  output [31:0] instruction2_out
);

  wire En1;

  not not_1 (En1, NOP);
  Register #(.width(1)) u_NOP (.D(NOP), .Q(NOP2_out), .clk(CLK), .clr(squash2));  // open: en
  Register #(.width(4)) Opcode (.D(Opcode2), .en(En1), .Q(Opcode2_out), .clk(CLK), .clr(squash2));
  Register #(.width(32)) Ry (.D(Ry_2), .en(En1), .Q(Ry_2_out), .clk(CLK), .clr(squash2));
  Register #(.width(32)) Rz (.D(Rz___Rx_2), .en(En1), .Q(Rz___Rx_2_out), .clk(CLK), .clr(squash2));
  Register #(.width(20)) Offset (.D(Offset2), .en(En1), .Q(Offset2_out), .clk(CLK), .clr(squash2));
  Register #(.width(32)) u_PC (.D(PC), .en(En1), .Q(PC2_out), .clk(CLK), .clr(squash2));
  Register #(.width(4)) Rx (.D(Rx2), .en(En1), .Q(Rx_out), .clk(CLK), .clr(squash2));
  Register #(.width(4)) u_Ry_2 (.D(Ry2), .en(En1), .Q(Ry2_out), .clk(CLK), .clr(squash2));
  Register #(.width(32)) ins (.D(instruction2), .en(En1), .Q(instruction2_out), .clk(CLK), .clr(squash2));

  // Other names for the same wires on the sheet: En2 = En1; En3 = En1; En4 = En1; En5 = En1; En6 = En1
endmodule

module EX_MEM_Buffer (
  input  NOP,
  input  [3:0] Opcode3,
  input  [31:0] Result3,
  input  [23:0] Address3,
  input  [3:0] Rx3,
  input  [3:0] Ry3,
  input  [31:0] Rx_3,
  input  [31:0] PC3,
  input  [31:0] mem_ins3,
  input  CLK,
  output NOP_2,
  output [3:0] Opcode3_out,
  output [31:0] Result3_out,
  output [23:0] Address3_out,
  output [3:0] Rx3_out,
  output [3:0] Ry_out,
  output [31:0] Rx_3_out,
  output [31:0] PC3_out,
  output [31:0] mem_ins3_out
);

  Register #(.width(1)) u_NOP (.D(NOP), .Q(NOP_2), .clk(CLK));  // open: en, clr
  Register #(.width(4)) Opcode (.D(Opcode3), .Q(Opcode3_out), .clk(CLK));  // open: en, clr
  Register #(.width(32)) Rsult (.D(Result3), .Q(Result3_out), .clk(CLK));  // open: en, clr
  Register #(.width(24)) Opcode_2 (.D(Address3), .Q(Address3_out), .clk(CLK));  // open: en, clr
  Register #(.width(4)) Rx (.D(Rx3), .Q(Rx3_out), .clk(CLK));  // open: en, clr
  Register #(.width(4)) Ry (.D(Ry3), .Q(Ry_out), .clk(CLK));  // open: en, clr
  Register #(.width(32)) Rx_2 (.D(Rx_3), .Q(Rx_3_out), .clk(CLK));  // open: en, clr
  Register #(.width(32)) PC (.D(PC3), .Q(PC3_out), .clk(CLK));  // open: en, clr
  Register #(.width(32)) mem_ins (.D(mem_ins3), .Q(mem_ins3_out), .clk(CLK));  // open: en, clr
endmodule

module MEM_WB_Buffer (
  input  NOP4,
  input  [3:0] Opcode4,
  input  [31:0] D4,
  input  [3:0] Rx4,
  input  [3:0] Ry4,
  input  [31:0] Rx_4,
  input  [31:0] PC4,
  input  [31:0] ins4,
  input  CLK,
  output NOP4_out,
  output [3:0] Opcode4_out,
  output [31:0] D4_out,
  output [3:0] Rx4_out,
  output [3:0] Ry4_out,
  output [31:0] Rx_4_out,
  output [31:0] PC4_out,
  output [31:0] ins4_out
);

  Register #(.width(1)) NOP (.D(NOP4), .Q(NOP4_out), .clk(CLK));  // open: en, clr
  Register #(.width(4)) Opcode (.D(Opcode4), .Q(Opcode4_out), .clk(CLK));  // open: en, clr
  Register #(.width(32)) D (.D(D4), .Q(D4_out), .clk(CLK));  // open: en, clr
  Register #(.width(4)) Rx (.D(Rx4), .Q(Rx4_out), .clk(CLK));  // open: en, clr
  Register #(.width(4)) Ry (.D(Ry4), .Q(Ry4_out), .clk(CLK));  // open: en, clr
  Register #(.width(32)) Rx_2 (.D(Rx_4), .Q(Rx_4_out), .clk(CLK));  // open: en, clr
  Register #(.width(32)) PC (.D(PC4), .Q(PC4_out), .clk(CLK));  // open: en, clr
  Register #(.width(32)) ins (.D(ins4), .Q(ins4_out), .clk(CLK));  // open: en, clr
endmodule

module ALU (
  input  [1:0] FUNC,
  input  [31:0] A,
  input  [31:0] B,
  output [31:0] OUT
);

  wire [31:0] adder_1_out, adder_2_out, nand_1_out, subtractor_1_out;

  Adder #(.width(32)) adder_1 (.a(A), .b(B), .out(adder_1_out), .cin(1'b0));  // open: cout
  assign nand_1_out = ~(A & B);  // NAND_Gate nand_1, 32 bits wide
  Subtractor #(.width(32)) subtractor_1 (.a(A), .b(B), .out(subtractor_1_out), .bin(1'b0));  // open: bout
  Adder #(.width(32)) adder_2 (.a(A), .b({32{1'b0}}), .out(adder_2_out), .cin(1'b1));  // open: cout
  Multiplexer #(.select(2), .width(32), .disabled(0), .enable("false")) multiplexer_1 (
    .in0(adder_1_out), .in1(nand_1_out), .in2(subtractor_1_out), .in3(adder_2_out), .out(OUT), .sel(FUNC));

  // Notes on the sheet:
  //   DO NOT MODIFY THIS
endmodule

module ID_RR_Controller (
  input  [3:0] Opcode,
  output Rx_Rz
);

  ROM #(.addrWidth(4), .dataWidth(1)) rom_1 (.addr(Opcode), .data(Rx_Rz));  // open: sel

  // Notes on the sheet:
  //   contents of rom_1 (hex, n*v repeats v):
  //   4*0 1 1 1
endmodule

module EX_Controller (
  input  NOP,
  input  [3:0] Opcode,
  output Offset_Rz,
  output jalr,
  output chkz,
  output [1:0] Func
);

  wire not_1_out;
  wire [4:0] rom_1_data;

  ROM #(.addrWidth(4), .dataWidth(5)) rom_1 (.addr(Opcode), .data(rom_1_data));  // open: sel
  not not_1 (not_1_out, NOP);
  assign Offset_Rz = not_1_out ? rom_1_data[4] : 1'bz;  // Controlled_Buffer controlled_buffer_1
  assign jalr = not_1_out ? rom_1_data[3] : 1'bz;  // Controlled_Buffer controlled_buffer_2
  assign chkz = not_1_out ? rom_1_data[2] : 1'bz;  // Controlled_Buffer controlled_buffer_3
  assign Func = not_1_out ? rom_1_data[1:0] : 2'bz;  // Controlled_Buffer controlled_buffer_4

  // Notes on the sheet:
  //   contents of rom_1 (hex, n*v repeats v):
  //   0 1 10 10 10 6 8
endmodule

module MEM_Controller (
  input  NOP,
  input  [3:0] Opcode,
  output mem_address,
  output mem_res,
  output rx_val,
  output WrMem,
  output LdMem
);

  wire not_1_out;
  wire [4:0] rom_1_data;

  ROM #(.addrWidth(4), .dataWidth(5)) rom_1 (.addr(Opcode), .data(rom_1_data));  // open: sel
  not not_1 (not_1_out, NOP);
  assign mem_address = not_1_out ? rom_1_data[4] : 1'bz;  // Controlled_Buffer controlled_buffer_1
  assign mem_res = not_1_out ? rom_1_data[3] : 1'bz;  // Controlled_Buffer controlled_buffer_2
  assign rx_val = not_1_out ? rom_1_data[2] : 1'bz;  // Controlled_Buffer controlled_buffer_3
  assign WrMem = not_1_out ? rom_1_data[1] : 1'bz;  // Controlled_Buffer controlled_buffer_4
  assign LdMem = not_1_out ? rom_1_data[0] : 1'bz;  // Controlled_Buffer controlled_buffer_5

  // Notes on the sheet:
  //   contents of rom_1 (hex, n*v repeats v):
  //   8 8 8 11 16
endmodule

module WB_Controller (
  input  NOP,
  input  [3:0] Opcode,
  output halt,
  output PC_DATA,
  output WrEn,
  output WB_Ry
);

  wire not_1_out;
  wire [3:0] rom_1_data;

  not not_1 (not_1_out, NOP);
  ROM #(.addrWidth(4), .dataWidth(4)) rom_1 (.addr(Opcode), .data(rom_1_data));  // open: sel
  assign halt = not_1_out ? rom_1_data[3] : 1'bz;  // Controlled_Buffer controlled_buffer_1
  assign PC_DATA = not_1_out ? rom_1_data[2] : 1'bz;  // Controlled_Buffer controlled_buffer_2
  assign WrEn = not_1_out ? rom_1_data[1] : 1'bz;  // Controlled_Buffer controlled_buffer_3
  assign WB_Ry = not_1_out ? rom_1_data[0] : 1'bz;  // Controlled_Buffer controlled_buffer_4

  // Notes on the sheet:
  //   contents of rom_1 (hex, n*v repeats v):
  //   4*2 0 0 5 8
endmodule

module forwarding_unit (
  input  [3:0] RDReg_1,
  input  [3:0] RDReg_2,
  input  [31:0] EX_Instruction,
  input  [31:0] EX_INPUT,
  input  [31:0] MEM_Instruction,
  input  [31:0] MEM_INPUT,
  input  [31:0] WB_Instruction,
  input  [31:0] WB_INPUT,
  output STALL,
  output _1,
  output [31:0] _1_2,
  output [31:0] _2,
  output _2_2
);

  wire _1E, _1M, _1W, _2E, _2M, _2W, and_1_out, and_2_out, and_3_out, and_4_out, comparator_1_lt,
       comparator_2_lt, comparator_3_lt, comparator_4_eq, comparator_5_eq, comparator_6_eq, comparator_7_eq,
       comparator_8_eq, comparator_9_eq, decoder_1_out0, decoder_1_out1, decoder_1_out2, decoder_1_out4,
       decoder_1_out5, decoder_1_out6, decoder_1_out7, decoder_2_out0, decoder_2_out1, decoder_2_out2,
       decoder_2_out3, decoder_2_out4, decoder_2_out5, decoder_2_out6, decoder_2_out7, decoder_3_out0,
       decoder_3_out1, decoder_3_out2, decoder_3_out3, decoder_3_out4, decoder_3_out5, decoder_3_out6,
       decoder_3_out7, multiplexer_1_out, multiplexer_4_out, multiplexer_7_out, or_1_out, or_2_out, or_3_out,
       or_4_out, or_5_out, or_6_out, or_7_out, or_8_out;
  wire [1:0] priority_encoder_1_out, priority_encoder_2_out;
  wire [31:0] controlled_buffer_1_out, controlled_buffer_2_out, controlled_buffer_3_out,
       controlled_buffer_4_out, controlled_buffer_5_out, controlled_buffer_6_out, controlled_buffer_7_out,
       controlled_buffer_8_out, controlled_buffer_9_out, undriven;

  Comparator #(.width(32)) comparator_1 (.a({32{1'b0}}), .b(EX_Instruction), .lt(comparator_1_lt));  // open: gt, eq
  Comparator #(.width(32)) comparator_2 (.a({32{1'b0}}), .b(MEM_Instruction), .lt(comparator_2_lt));  // open: gt, eq
  Comparator #(.width(32)) comparator_3 (.a({32{1'b0}}), .b(WB_Instruction), .lt(comparator_3_lt));  // open: gt, eq
  Comparator #(.width(4)) comparator_4 (.a(EX_Instruction[27:24]), .b(RDReg_1), .eq(comparator_4_eq));  // open: gt, lt
  Comparator #(.width(4)) comparator_5 (.a(EX_Instruction[27:24]), .b(RDReg_2), .eq(comparator_5_eq));  // open: gt, lt
  assign controlled_buffer_1_out = or_3_out ? EX_INPUT : 32'bz;  // Controlled_Buffer controlled_buffer_1
  assign controlled_buffer_2_out = or_4_out ? MEM_INPUT : 32'bz;  // Controlled_Buffer controlled_buffer_2
  Comparator #(.width(4)) comparator_6 (.a(WB_Instruction[27:24]), .b(RDReg_1), .eq(comparator_6_eq));  // open: gt, lt
  Comparator #(.width(4)) comparator_7 (.a(WB_Instruction[27:24]), .b(RDReg_2), .eq(comparator_7_eq));  // open: gt, lt
  assign controlled_buffer_3_out = or_5_out ? WB_INPUT : 32'bz;  // Controlled_Buffer controlled_buffer_3
  Multiplexer multiplexer_1 (.in0(comparator_3_lt), .in1(1'b0), .out(multiplexer_1_out), .sel(or_8_out));  // open: en
  Multiplexer multiplexer_2 (.in0(1'b0), .in1(comparator_6_eq), .out(_1W), .sel(multiplexer_1_out));  // open: en
  Multiplexer multiplexer_3 (.in0(1'b0), .in1(comparator_7_eq), .out(_2W), .sel(multiplexer_1_out));  // open: en
  Multiplexer multiplexer_4 (.in0(comparator_1_lt), .in1(1'b0), .out(multiplexer_4_out), .sel(or_6_out));  // open: en
  Multiplexer multiplexer_5 (.in0(1'b0), .in1(comparator_4_eq), .out(_1E), .sel(multiplexer_4_out));  // open: en
  Multiplexer multiplexer_6 (.in0(1'b0), .in1(comparator_5_eq), .out(_2E), .sel(multiplexer_4_out));  // open: en
  Multiplexer multiplexer_7 (.in0(comparator_2_lt), .in1(1'b0), .out(multiplexer_7_out), .sel(or_7_out));  // open: en
  Comparator #(.width(4)) comparator_8 (.a(MEM_Instruction[27:24]), .b(RDReg_1), .eq(comparator_8_eq));  // open: gt, lt
  Comparator #(.width(4)) comparator_9 (.a(MEM_Instruction[27:24]), .b(RDReg_2), .eq(comparator_9_eq));  // open: gt, lt
  or or_1 (or_1_out, _2E, _2M);
  Multiplexer multiplexer_8 (.in0(1'b0), .in1(comparator_8_eq), .out(_1M), .sel(multiplexer_7_out));  // open: en
  Multiplexer multiplexer_9 (.in0(1'b0), .in1(comparator_9_eq), .out(_2M), .sel(multiplexer_7_out));  // open: en
  or or_2 (or_2_out, _1E, _1M);
  Decoder #(.select(3)) decoder_1 (
    .out0(decoder_1_out0), .out1(decoder_1_out1), .out2(decoder_1_out2), .out3(STALL), .out4(decoder_1_out4),
    .out5(decoder_1_out5), .out6(decoder_1_out6), .out7(decoder_1_out7), .sel(EX_Instruction[30:28]));  // open: en
  or or_3 (or_3_out, decoder_1_out0, decoder_1_out1, decoder_1_out2);
  assign controlled_buffer_4_out = _1E ? controlled_buffer_1_out : 32'bz;  // Controlled_Buffer controlled_buffer_4
  assign controlled_buffer_5_out = _2E ? controlled_buffer_1_out : 32'bz;  // Controlled_Buffer controlled_buffer_5
  Decoder #(.select(3)) decoder_2 (
    .out0(decoder_2_out0), .out1(decoder_2_out1), .out2(decoder_2_out2), .out3(decoder_2_out3),
    .out4(decoder_2_out4), .out5(decoder_2_out5), .out6(decoder_2_out6), .out7(decoder_2_out7),
    .sel(MEM_Instruction[30:28]));  // open: en
  or or_4 (or_4_out, decoder_2_out0, decoder_2_out1, decoder_2_out2, decoder_2_out3);
  and and_1 (and_1_out, ~_1E, _1M);  // AND_Gate
  assign controlled_buffer_6_out = and_1_out ? controlled_buffer_2_out : 32'bz;  // Controlled_Buffer controlled_buffer_6
  and and_2 (and_2_out, ~_2E, _2M);  // AND_Gate
  assign controlled_buffer_7_out = and_2_out ? controlled_buffer_2_out : 32'bz;  // Controlled_Buffer controlled_buffer_7
  Decoder #(.select(3)) decoder_3 (
    .out0(decoder_3_out0), .out1(decoder_3_out1), .out2(decoder_3_out2), .out3(decoder_3_out3),
    .out4(decoder_3_out4), .out5(decoder_3_out5), .out6(decoder_3_out6), .out7(decoder_3_out7),
    .sel(WB_Instruction[30:28]));  // open: en
  or or_5 (or_5_out, decoder_3_out0, decoder_3_out1, decoder_3_out2, decoder_3_out3);
  and and_3 (and_3_out, ~or_2_out, _1W);  // AND_Gate
  assign controlled_buffer_8_out = and_3_out ? controlled_buffer_3_out : 32'bz;  // Controlled_Buffer controlled_buffer_8
  and and_4 (and_4_out, ~or_1_out, _2W);  // AND_Gate
  assign controlled_buffer_9_out = and_4_out ? controlled_buffer_3_out : 32'bz;  // Controlled_Buffer controlled_buffer_9
  or or_6 (or_6_out, decoder_1_out4, decoder_1_out5, decoder_1_out6, decoder_1_out7);
  or or_7 (or_7_out, decoder_2_out5, decoder_2_out6, decoder_2_out7, decoder_2_out4);
  or or_8 (or_8_out, decoder_3_out4, decoder_3_out5, decoder_3_out6, decoder_3_out7);
  Priority_Encoder #(.select(2)) priority_encoder_1 (
    .in1(_1W), .in2(_1M), .in3(_1E), .out(priority_encoder_1_out));  // open: in0, gs, en_out, en_in
  or or_9 (_1, _1W, _1M, _1E);
  Priority_Encoder #(.select(2)) priority_encoder_2 (
    .in1(_2W), .in2(_2M), .in3(_2E), .out(priority_encoder_2_out));  // open: in0, gs, en_out, en_in
  or or_10 (_2_2, _2W, _2M, _2E);
  Multiplexer #(.select(2), .width(32)) multiplexer_10 (
    .in1(controlled_buffer_8_out), .in2(controlled_buffer_6_out), .in3(controlled_buffer_4_out), .out(_1_2),
    .sel(priority_encoder_1_out));  // open: in0, en
  Multiplexer #(.select(2), .width(32)) multiplexer_11 (
    .in0(undriven), .in1(controlled_buffer_9_out), .in2(controlled_buffer_7_out),
    .in3(controlled_buffer_5_out), .out(_2), .sel(priority_encoder_2_out));  // open: en

  // Other names for the same wires on the sheet: R1[3:0] = RDReg_1; R2[3:0] = RDReg_2

  // Notes on the sheet:
  //   op
  //   Rx
  //   op
  //   Rx
  //   op
  //   Rx
endmodule

module buffer (
  input  squash,
  input  NOP,
  input  [31:0] PC,
  input  [31:0] In,
  input  Clk,
  output NOP_out,
  output [31:0] PC_out,
  output [31:0] Out
);

  wire not_1_out;

  not not_1 (not_1_out, NOP);
  Register #(.width(1)) u_NOP (.D(NOP), .Q(NOP_out), .clk(Clk));  // open: en, clr
  Register #(.width(32)) u_PC (.D(PC), .en(not_1_out), .Q(PC_out), .clk(Clk), .clr(squash));
  Register #(.width(32)) register_1 (.D(In), .en(not_1_out), .Q(Out), .clk(Clk), .clr(squash));
endmodule
