// Logisim project organizasyonlab09.circ as structural Verilog: 1 circuit, main circuit main
module main (
  input  DWrite,
  input  [1:0] dRegSel,
  input  [7:0] WriteDataVal,
  input  [1:0] srcRegSel,
  output [7:0] out_5,
  output out_6,
  output [7:0] out_7,
  output Negative
);

  wire clock_1_out, demultiplexer_1_out0, demultiplexer_1_out1, demultiplexer_1_out2, demultiplexer_1_out3,
       or_1_out;
  wire [7:0] register_1_q, register_2_q, register_3_q, register_4_q;

  Demultiplexer #(.select(2), .enable("false")) demultiplexer_1 (
    .out0(demultiplexer_1_out0), .out1(demultiplexer_1_out1), .out2(demultiplexer_1_out2),
    .out3(demultiplexer_1_out3), .in(DWrite), .sel(dRegSel));
  Register register_1 (.D(WriteDataVal), .en(demultiplexer_1_out0), .Q(register_1_q), .clk(clock_1_out));  // open: clr
  Register register_2 (.D(WriteDataVal), .en(demultiplexer_1_out1), .Q(register_2_q), .clk(clock_1_out));  // open: clr
  Register register_3 (.D(WriteDataVal), .en(demultiplexer_1_out2), .Q(register_3_q), .clk(clock_1_out));  // open: clr
  Register register_4 (.D(WriteDataVal), .en(demultiplexer_1_out3), .Q(register_4_q), .clk(clock_1_out));  // open: clr
  Clock clock_1 (.out(clock_1_out));
  Multiplexer #(.select(2), .width(8), .enable("false")) multiplexer_1 (
    .in0(register_1_q), .in1(register_2_q), .in2(register_3_q), .in3(register_4_q),
    .out({Negative, out_5[6:0]}), .sel(dRegSel));
  Multiplexer #(.select(2), .width(8), .enable("false")) multiplexer_2 (
    .in0(register_1_q), .in1(register_2_q), .in2(register_3_q), .in3(register_4_q), .out(out_7),
    .sel(srcRegSel));
  or or_1 (or_1_out, out_5[0], out_5[1], out_5[2], out_5[3], out_5[4], out_5[5], out_5[6], Negative);
  not not_1 (out_6, or_1_out);

  assign out_5[7] = Negative;

  // Other names for the same wires on the sheet: drs[1:0] = dRegSel
endmodule
