// Logisim project LC-2200-16.circ as structural Verilog: 4 circuits, main circuit main
module main (
);

  wire ALUHi, ALULo, chkZ, CLK, DrALU, DrMEM, DrOFF, DrPC, DrREG, LdA, LdB, LdIR, LdMAR, LdPC, LdZ, OPTest,
       RegSelHi, RegSelLo, WrMEM, WrREG, Z;
  wire [2:0] OP;
  wire [3:0] datapath_1_rx, datapath_1_ry, datapath_1_rz, multiplexer_1_out;

  DataPath datapath_1 (
    .CLK(CLK), .LdA(LdA), .WrREG(WrREG), .LdMAR(LdMAR), .LdZ(LdZ), .LdPC(LdPC), .LdB(LdB),
    .regno(multiplexer_1_out), .WrMEM(WrMEM), .DrPC(DrPC), .func({ALUHi, ALULo}), .DrREG(DrREG),
    .DrMEM(DrMEM), .LdIR(LdIR), .DrALU(DrALU), .DrOFF(DrOFF), .Z(Z), .RX(datapath_1_rx), .RY(datapath_1_ry),
    .RZ(datapath_1_rz), .OP(OP));
  Clock clock_1 (.out(CLK));
  Multiplexer #(.select(2), .width(4), .enable("false")) multiplexer_1 (
    .in0(datapath_1_rx), .in2(datapath_1_ry), .in3(datapath_1_rz), .out(multiplexer_1_out),
    .sel({RegSelHi, RegSelLo}));  // open: in1
  Microcontroller microcontroller_1 (
    .OP(OP), .CLK(CLK), .Z(Z), .DrREG(DrREG), .LdPC(LdPC), .WrREG(WrREG), .ALULo(ALULo), .DrMEM(DrMEM),
    .LdIR(LdIR), .WrMEM(WrMEM), .ALUHi(ALUHi), .DrALU(DrALU), .LdMAR(LdMAR), .RegSelLo(RegSelLo),
    .OPTest(OPTest), .DrPC(DrPC), .LdA(LdA), .RegSelHi(RegSelHi), .chkZ(chkZ), .DrOFF(DrOFF), .LdB(LdB),
    .LdZ(LdZ));
endmodule

module ALU_16bits (
  input  [15:0] A,
  input  [15:0] B,
  input  [1:0] selector,
  output [15:0] Out
);

  wire [15:0] adder_1_out, adder_2_out, adder_3_out, nand_1_out;

  Adder #(.width(16)) adder_1 (.a(A), .b(B), .out(adder_1_out));  // open: cin, cout
  assign nand_1_out = ~(A & B);  // NAND_Gate nand_1, 16 bits wide
  Adder #(.width(16)) adder_2 (.a(A), .b(B), .out(adder_2_out));  // open: cin, cout
  Adder #(.width(16)) adder_3 (.a(A), .b(16'h1), .out(adder_3_out));  // open: cin, cout
  Multiplexer #(.select(2), .width(16), .enable("false")) multiplexer_1 (
    .in0(adder_1_out), .in1(nand_1_out), .in2(adder_2_out), .in3(adder_3_out), .out(Out), .sel(selector));
endmodule

module DataPath (
  input  LdA,
  input  WrREG,
  input  LdMAR,
  input  LdPC,
  input  LdB,
  input  [3:0] regno,
  input  WrMEM,
  input  LdIR,
  input  DrPC,
  input  DrOFF,
  input  [1:0] func,
  input  DrREG,
  input  DrMEM,
  input  DrALU,
  input  CLK,
  input  LdZ,
  output Z,
  output [3:0] RX,
  output [3:0] RY,
  output [3:0] RZ,
  output [2:0] OP
);

  wire button_1_out, button_2_out, button_3_out, comparator_1_eq, comparator_2_eq, not_1_out;
  wire [4:4] IR_q;
  wire [15:0] A_q, alu_16bits_1_out, B_q, bit_extender_1_out, controlled_buffer_1_out, MAR_q,
       multiplexer_1_out, PC_q, ram_1_data, ram_2_data;

  Register #(.width(16)) PC (.D(controlled_buffer_1_out), .en(LdPC), .Q(PC_q), .clk(CLK), .clr(button_1_out));
  Button button_1 (.out(button_1_out));
  assign controlled_buffer_1_out = DrPC ? PC_q : 16'bz;  // Controlled_Buffer controlled_buffer_1
  Register #(.width(16)) A (.en(LdA), .Q(A_q), .clk(CLK));  // open: D, clr
  Comparator #(.width(16)) comparator_1 (.a(controlled_buffer_1_out), .eq(comparator_1_eq));  // open: b, gt, lt
  ALU_16bits alu_16bits_1 (.selector(func), .Out(alu_16bits_1_out), .A(A_q), .B(B_q));
  assign controlled_buffer_1_out = DrALU ? alu_16bits_1_out : 16'bz;  // Controlled_Buffer controlled_buffer_2
  Register #(.width(1)) u_Z (.D(comparator_1_eq), .en(LdZ), .Q(Z), .clk(CLK));  // open: clr
  Register #(.width(16)) B (.en(LdB), .Q(B_q), .clk(CLK));  // open: D, clr
  Comparator #(.width(4)) comparator_2 (.a(regno), .b(4'b0000), .eq(comparator_2_eq));  // open: gt, lt
  Button button_2 (.out(button_2_out));
  not not_1 (not_1_out, comparator_2_eq);
  RAM #(.addrWidth(4), .dataWidth(16), .bus("separate")) ram_1 (
    .addr(regno), .din(controlled_buffer_1_out), .data(ram_1_data), .str(WrREG), .clk(CLK), .clr(button_2_out));  // open: sel, ld
  Multiplexer #(.width(16), .enable("false")) multiplexer_1 (
    .in0({16{1'b0}}), .in1(ram_1_data), .out(multiplexer_1_out), .sel(not_1_out));
  assign controlled_buffer_1_out = DrREG ? multiplexer_1_out : 16'bz;  // Controlled_Buffer controlled_buffer_3
  Register #(.width(16)) MAR (.D(controlled_buffer_1_out), .en(LdMAR), .Q(MAR_q), .clk(CLK));  // open: clr
  RAM #(.addrWidth(16), .dataWidth(16), .bus("separate")) ram_2 (
    .addr(MAR_q), .din(controlled_buffer_1_out), .data(ram_2_data), .str(WrMEM), .clk(CLK), .clr(button_3_out));  // open: sel, ld
  Button button_3 (.out(button_3_out));
  assign controlled_buffer_1_out = DrMEM ? ram_2_data : 16'bz;  // Controlled_Buffer controlled_buffer_4
  Register #(.width(16)) IR (
    .D(controlled_buffer_1_out), .en(LdIR), .Q({OP, RX, RY, IR_q[4], RZ}), .clk(CLK));  // open: clr
  assign bit_extender_1_out = {{11{IR_q[4]}}, {IR_q[4], RZ}};  // Bit_Extender bit_extender_1
  assign controlled_buffer_1_out = DrOFF ? bit_extender_1_out : 16'bz;  // Controlled_Buffer controlled_buffer_5

  // Notes on the sheet:
  //   REGISTER fILE
  //   MEMORY
endmodule

module Microcontroller (
  input  [2:0] OP,
  input  CLK,
  input  Z,
  output DrREG,
  output LdPC,
  output WrREG,
  output ALULo,
  output DrMEM,
  output LdIR,
  output WrMEM,
  output ALUHi,
  output DrALU,
  output LdMAR,
  output RegSelLo,
  output OPTest,
  output DrPC,
  output LdA,
  output RegSelHi,
  output chkZ,
  output DrOFF,
  output LdB,
  output LdZ
);

  wire button_1_out;
  wire [5:0] multiplexer_1_out, nState, OPdata, State, Zdata;

  ROM #(.addrWidth(6), .dataWidth(25)) rom_1 (
    .addr(State),
    .data({chkZ, OPTest, ALUHi, ALULo, RegSelHi, RegSelLo, WrMEM, WrREG, LdZ, LdB, LdA, LdMAR, LdIR, LdPC, DrOFF, DrPC, DrALU, DrMEM, DrREG, nState}));  // open: sel
  Multiplexer #(.select(2), .width(6), .enable("false")) multiplexer_1 (
    .in0(nState), .in1(OPdata), .in2(Zdata), .out(multiplexer_1_out), .sel({chkZ, OPTest}));  // open: in3
  ROM #(.addrWidth(3), .dataWidth(6)) rom_2 (.addr(OP), .data(OPdata));  // open: sel
  Register #(.width(6)) State_Register (.D(multiplexer_1_out), .Q(State), .clk(CLK), .clr(button_1_out));  // open: en
  ROM #(.addrWidth(2), .dataWidth(6)) rom_3 (.addr({1'b0, Z}), .data(Zdata));  // open: sel
  Button button_1 (.out(button_1_out));

  // Notes on the sheet:
  //   Main Rom
  //   Op Check ROM
  //   OnZ ROM
endmodule
