// Logisim project datapath.circ as structural Verilog: 4 circuits, main circuit main
module datapath (
  input  LdA,
  input  LdB,
  input  WrREG,
  input  LdMAR,
  input  LdPC,
  input  [1:0] func,
  input  [3:0] regno,
  input  WrMEM,
  input  LdIR,
  input  DrPC,
  input  DrALU,
  input  DrREG,
  input  DrMEM,
  input  DrOFF,
  input  CLK,
  input  LdZ,
  output Z,
  output [3:0] RX,
  output [3:0] RY,
  output [3:0] RZ,
  output [2:0] OP
);

  wire button_1_out, button_2_out, button_3_out, comparator_1_eq, comparator_2_eq, not_1_out;
  wire [4:4] IR_q;
  wire [15:0] A_q, alu_1_out, B_q, bit_extender_1_out, controlled_buffer_1_out, MAR_q, multiplexer_1_out,
       PC_q, ram_1_data, ram_2_data;

  Register #(.width(16)) PC (.D(controlled_buffer_1_out), .en(LdPC), .Q(PC_q), .clk(CLK), .clr(button_1_out));
  Button button_1 (.out(button_1_out));
  assign controlled_buffer_1_out = DrPC ? PC_q : 16'bz;  // Controlled_Buffer controlled_buffer_1
  Register #(.width(16)) A (.D(controlled_buffer_1_out), .en(LdA), .Q(A_q), .clk(CLK));  // open: clr
  ALU alu_1 (.A(A_q), .B(B_q), .func(func), .out(alu_1_out));
  Register #(.width(1)) u_Z (.D(comparator_1_eq), .en(LdZ), .Q(Z), .clk(CLK));  // open: clr
  assign controlled_buffer_1_out = DrALU ? alu_1_out : 16'bz;  // Controlled_Buffer controlled_buffer_2
  Comparator #(.width(16)) comparator_1 (
    .a(controlled_buffer_1_out), .b({16{1'b0}}), .eq(comparator_1_eq));  // open: gt, lt
  Register #(.width(16)) B (.D(controlled_buffer_1_out), .en(LdB), .Q(B_q), .clk(CLK));  // open: clr
  Comparator #(.width(4)) comparator_2 (.a(regno), .b(4'b0000), .eq(comparator_2_eq));  // open: gt, lt
  RAM #(.addrWidth(4), .dataWidth(16), .bus("separate")) ram_1 (
    .addr(regno), .din(controlled_buffer_1_out), .data(ram_1_data), .str(WrREG), .clk(CLK), .clr(button_2_out));  // open: sel, ld
  Button button_2 (.out(button_2_out));
  not not_1 (not_1_out, comparator_2_eq);
  Multiplexer #(.width(16), .enable("false")) multiplexer_1 (
    .in0({16{1'b0}}), .in1(ram_1_data), .out(multiplexer_1_out), .sel(not_1_out));
  assign controlled_buffer_1_out = DrREG ? multiplexer_1_out : 16'bz;  // Controlled_Buffer controlled_buffer_3
  Register #(.width(16)) MAR (.D(controlled_buffer_1_out), .en(LdMAR), .Q(MAR_q), .clk(CLK));  // open: clr
  RAM #(.addrWidth(16), .dataWidth(16), .bus("separate")) ram_2 (
    .addr(MAR_q), .din(controlled_buffer_1_out), .data(ram_2_data), .str(WrMEM), .clk(CLK), .clr(button_3_out));  // open: sel, ld
  Button button_3 (.out(button_3_out));
  assign controlled_buffer_1_out = DrMEM ? ram_2_data : 16'bz;  // Controlled_Buffer controlled_buffer_4
  Register #(.width(16)) IR (
    .D(controlled_buffer_1_out), .en(LdIR), .Q({OP, RX, RY, IR_q[4], RZ}), .clk(CLK));  // open: clr
  assign bit_extender_1_out = {{11{IR_q[4]}}, {IR_q[4], RZ}};  // Bit_Extender bit_extender_1
  assign controlled_buffer_1_out = DrOFF ? bit_extender_1_out : 16'bz;  // Controlled_Buffer controlled_buffer_5

  // Notes on the sheet:
  //   LC2200 Datapath, by Tim Martin
  //   Register File
  //   Memory
endmodule

module ALU (
  input  [15:0] A,
  input  [15:0] B,
  input  [1:0] func,
  output [15:0] out
);

  wire [15:0] adder_1_out, adder_2_out, nand_1_out, subtractor_1_out;

  Adder #(.width(16)) adder_1 (.a(A), .b(B), .out(adder_1_out));  // open: cin, cout
  assign nand_1_out = ~(A & B);  // NAND_Gate nand_1, 16 bits wide
  Subtractor #(.width(16)) subtractor_1 (.a(A), .b(B), .out(subtractor_1_out));  // open: bin, bout
  Adder #(.width(16)) adder_2 (.a(A), .b(16'h1), .out(adder_2_out));  // open: cin, cout
  Multiplexer #(.select(2), .width(16), .enable("false")) multiplexer_1 (
    .in0(adder_1_out), .in1(nand_1_out), .in2(subtractor_1_out), .in3(adder_2_out), .out(out), .sel(func));

  // Notes on the sheet:
  //   ALU, by Tim Martin
endmodule

module microcontrol_unit (
  input  [2:0] OP,
  input  Z,
  input  CLK,
  output LdPC,
  output DrReg,
  output LdIR,
  output DrMEM,
  output LdMAR,
  output DrALU,
  output LdA,
  output DrPC,
  output LdB,
  output WrREG,
  output RegSelLo,
  output ALULo,
  output OPTest,
  output DrOFF,
  output LdZ,
  output WrMEM,
  output RegSelHi,
  output ALUHi,
  output chkZ
);

  wire button_1_out;
  wire [5:0] multiplexer_1_out, nState, OPdata, State, Zdata;

  ROM #(.addrWidth(6), .dataWidth(25)) rom_1 (
    .addr(State),
    .data({chkZ, OPTest, ALUHi, ALULo, RegSelHi, RegSelLo, WrMEM, WrREG, LdZ, LdB, LdA, LdMAR, LdIR, LdPC, DrOFF, DrPC, DrALU, DrMEM, DrReg, nState}));  // open: sel
  ROM #(.addrWidth(3), .dataWidth(6)) rom_2 (.addr(OP), .data(OPdata));  // open: sel
  ROM #(.addrWidth(2), .dataWidth(6)) rom_3 (.addr({1'b0, Z}), .data(Zdata));  // open: sel
  Multiplexer #(.select(2), .width(6), .enable("false")) multiplexer_1 (
    .in0(nState), .in1(OPdata), .in2(Zdata), .out(multiplexer_1_out), .sel({chkZ, OPTest}));  // open: in3
  Register #(.width(6)) State_Register (.D(multiplexer_1_out), .Q(State), .clk(CLK), .clr(button_1_out));  // open: en
  Button button_1 (.out(button_1_out));

  // Notes on the sheet:
  //   Main ROM
  //   OpCheck ROM
  //   OnZ ROM
  //   contents of rom_1 (hex, n*v repeats v):
  //   6201 1082 e00900 84044 108045 20100 84047 8408 20100 8404a 10804b 220100 8404d 840e 210f 20080 84051
  //   8412 2113 40040 4055 88056 1410100 6202 4219 841a 900 a021c 840 1d
  //   contents of rom_2 (hex, n*v repeats v):
  //   3 9 6 c 10 14 1b 1d
  //   contents of rom_3 (hex, n*v repeats v):
  //   17 18
  //   Microcontrol Unit, by Tim Martin
endmodule

module main (
);

  wire ALUHi, ALULo, chkZ, CLK, DrALU, DrMEM, DrOFF, DrPC, DrREG, LdA, LdB, LdIR, LdMAR, LdPC, LdZ, OPTest,
       RegSelHi, RegSelLo, WrMEM, WrREG, Z;
  wire [2:0] OP;
  wire [3:0] datapath_1_rx, datapath_1_ry, datapath_1_rz, multiplexer_1_out;

  datapath datapath_1 (
    .LdA(LdA), .LdB(LdB), .WrREG(WrREG), .LdMAR(LdMAR), .LdPC(LdPC), .func({ALUHi, ALULo}),
    .regno(multiplexer_1_out), .WrMEM(WrMEM), .LdIR(LdIR), .DrPC(DrPC), .DrALU(DrALU), .DrREG(DrREG),
    .DrMEM(DrMEM), .DrOFF(DrOFF), .CLK(CLK), .LdZ(LdZ), .Z(Z), .RX(datapath_1_rx), .RY(datapath_1_ry),
    .RZ(datapath_1_rz), .OP(OP));
  Clock clock_1 (.out(CLK));
  Multiplexer #(.select(2), .width(4), .enable("false")) multiplexer_1 (
    .in0(datapath_1_rx), .in1(datapath_1_ry), .in2(datapath_1_rz), .out(multiplexer_1_out),
    .sel({RegSelHi, RegSelLo}));  // open: in3
  microcontrol_unit microcontrol_unit_1 (
    .OP(OP), .Z(Z), .CLK(CLK), .LdPC(LdPC), .DrReg(DrREG), .LdIR(LdIR), .DrMEM(DrMEM), .LdMAR(LdMAR),
    .DrALU(DrALU), .LdA(LdA), .DrPC(DrPC), .LdB(LdB), .WrREG(WrREG), .RegSelLo(RegSelLo), .ALULo(ALULo),
    .OPTest(OPTest), .DrOFF(DrOFF), .LdZ(LdZ), .WrMEM(WrMEM), .RegSelHi(RegSelHi), .ALUHi(ALUHi), .chkZ(chkZ));

  // Notes on the sheet:
  //   Main Circuit, by Tim Martin
endmodule
